// Logisim project H1.circ as structural Verilog: 10 circuits, main circuit P1
module P1 (
  input  I3,
  input  I2,
  input  I1,
  input  I0,
  output A,
  output B,
  output C,
  output D,
  output E,
  output F,
  output G,
  output H,
  output I,
  output J,
  output K,
  output L,
  output M,
  output N,
  output O,
  output P
);

  wire A_out, B_out, C_out, E_out;

  not u_E (E_out, I3);
  not u_A (A_out, I2);
  not u_B (B_out, I1);
  not u_C (C_out, I0);
  and A_0 (A, C_out, B_out, A_out, E_out);
  and B_1 (B, I0, B_out, A_out, E_out);
  and C_2 (C, C_out, I1, A_out, E_out);
  and D_3 (D, I0, I1, A_out, E_out);
  and E_4 (E, C_out, B_out, I2, E_out);
  and F_5 (F, I0, B_out, I2, E_out);
  and G_6 (G, C_out, I1, I2, E_out);
  and H_7 (H, I0, I1, I2, E_out);
  and I_8 (I, C_out, B_out, A_out, I3);
  and J_9 (J, I0, B_out, A_out, I3);
  and K_10 (K, C_out, I1, A_out, I3);
  and L_11 (L, I0, I1, A_out, I3);
  and M_12 (M, C_out, B_out, I2, I3);
  and N_13 (N, I0, B_out, I2, I3);
  and O_14 (O, C_out, I1, I2, I3);
  and P_15 (P, I0, I1, I2, I3);

  // Notes on the sheet:
  //   PROBLEM 1: DECODER
  //   INPUT SECTION: Do not change anything here!
  //   You may only change the values of the inputs for testing using the hand tool.
  //   Do not introduce any other input or output pins.
  //   To your logic
  //   OUTPUT SECTION: Do not change anything here!
  //   Do not introduce any other input or output pins.
  //   From your logic
endmodule

module P2 (
  input  A,
  input  B,
  input  C,
  output X,
  output Y
);

  wire and_1_out, and_2_out, not_1_out, not_2_out, not_3_out;

  not not_1 (not_1_out, A);
  not not_2 (not_2_out, B);
  not not_3 (not_3_out, C);
  and and_1 (and_1_out, not_1_out, not_2_out, C);
  and and_2 (and_2_out, A, B, not_3_out);
  and and_3 (Y, A, not_2_out);
  or or_1 (X, and_1_out, and_2_out);

  // Notes on the sheet:
  //   PROBLEM 2: PROGRAMMABLE LOGIC ARRAY
  //   INPUT SECTION: Do not change anything here!
  //   You may only change the values of the inputs for testing using the hand tool.
  //   Do not introduce any other input or output pins.
  //   To your logic
  //   OUTPUT SECTION: Do not change anything here!
  //   Do not introduce any other input or output pins.
  //   From your logic
endmodule

module P3 (
  input  A,
  input  B,
  input  C,
  output X
);

  wire transistor_1_out, transistor_2_out, transistor_7_out, transistor_8_out;

  Transistor transistor_1 (.in(transistor_2_out), .out(transistor_1_out), .gate(A));
  Transistor transistor_2 (.in(1'b1), .out(transistor_2_out), .gate(A));
  Transistor transistor_3 (.in(1'b1), .out(transistor_2_out), .gate(C));
  Transistor transistor_4 (.in(transistor_2_out), .out(transistor_1_out), .gate(B));
  Transistor transistor_5 (.in(transistor_1_out), .out(X), .gate(C));
  Transistor transistor_6 (.in(transistor_2_out), .out(transistor_1_out), .gate(C));
  Transistor transistor_7 (.in(1'b1), .out(transistor_7_out), .gate(A));
  Transistor transistor_8 (.in(transistor_7_out), .out(transistor_8_out), .gate(C));
  Transistor transistor_9 (.in(transistor_7_out), .out(X), .gate(B));
  Transistor transistor_10 (.in(transistor_8_out), .out(X), .gate(A));

  // Other names for the same wires on the sheet: tA = A; tB = B; tC = C

  // Notes on the sheet:
  //   PROBLEM 3: SERIES-PARALLEL CIRCUITS OF TRANSISTORS
  //   RESERVED SECTION: Do not change anything here!
  //   You may only change the values of the inputs for testing using the hand tool.
  //   Do not introduce any other input or output pins.
  //   From your pull-down circuit
endmodule

module P4_Main (
  input  A4,
  input  A3,
  input  A2,
  input  A1,
  input  A0,
  output X4,
  output X3,
  output X2,
  output X1,
  output X0
);


  // Notes on the sheet:
  //   PROBLEM 4: 5-BIT INCREMENTER (Main)
  //   INPUT SECTION: Do not change anything here!
  //   You may only change the values of the inputs for testing using the hand tool.
  //   Do not introduce any other input or output pins.
  //   To your logic
  //   OUTPUT SECTION: Do not change anything here!
  //   Do not introduce any other input or output pins.
  //   From your logic
endmodule

module P4_IncrOneBit (
  input  Cin,
  input  A,
  output S,
  output Cout
);


  // Notes on the sheet:
  //   PROBLEM 4: 12-BIT INCREMENTER (IncrOneBit)
  //   INPUT SECTION: Do not change anything here!
  //   You may only change the values of the inputs for testing using the hand tool.
  //   Do not introduce any other input or output pins.
  //   To your logic
  //   OUTPUT SECTION: Do not change anything here!
  //   Do not introduce any other input or output pins.
  //   From your logic
endmodule

module P4_IncrBit0 (
  input  A,
  output S,
  output Cout
);


  // Notes on the sheet:
  //   PROBLEM 4: 12-BIT INCREMENTER (IncrBit0)
  //   INPUT SECTION: Do not change anything here!
  //   You may only change the values of the inputs for testing using the hand tool.
  //   Do not introduce any other input or output pins.
  //   To your logic
  //   OUTPUT SECTION: Do not change anything here!
  //   Do not introduce any other input or output pins.
  //   From your logic
endmodule

module P5_Main (
  input  A9,
  input  A8,
  input  A7,
  input  A6,
  input  A5,
  input  A4,
  input  A3,
  input  A2,
  input  A1,
  input  A0,
  output X9,
  output X8,
  output X7,
  output X6,
  output X5,
  output X4,
  output X3,
  output X2,
  output X1,
  output X0
);


  // Notes on the sheet:
  //   PROBLEM 5: 10-BIT LEFT NORMALIZER (Main)
  //   INPUT SECTION: Do not change anything here!
  //   You may only change the values of the inputs for testing using the hand tool.
  //   Do not introduce any other input or output pins.
  //   To your logic
  //   OUTPUT SECTION: Do not change anything here!
  //   Do not introduce any other input or output pins.
  //   From your logic
endmodule

module P5_LSH1 (
  input  [9:0] X,
  output [9:0] Y
);


  // Notes on the sheet:
  //   PROBLEM 5: 10-BIT LEFT NORMALIZER (LSH1)
  //   INPUT SECTION: Do not change anything here!
  //   You may only change the values of the inputs for testing using the hand tool.
  //   Do not introduce any other input or output pins.
  //   To your logic
  //   OUTPUT SECTION: Do not change anything here!
  //   Do not introduce any other input or output pins.
  //   From your logic
endmodule

module P5_Mux11 (
  input  S,
  input  [9:0] A,
  input  [9:0] B,
  output [9:0] X
);


  // Notes on the sheet:
  //   PROBLEM 5: 10-BIT LEFT NORMALIZER
  //   INPUT SECTION: Do not change anything here!
  //   You may only change the values of the inputs for testing using the hand tool.
  //   Do not introduce any other input or output pins.
  //   To your logic
  //   OUTPUT SECTION: Do not change anything here!
  //   Do not introduce any other input or output pins.
  //   From your logic
endmodule

module P5_CLSH1 (
  input  [9:0] X,
  output [9:0] Y
);


  // Notes on the sheet:
  //   PROBLEM 5: 10-BIT LEFT NORMALIZER (CLSH1)
  //   INPUT SECTION: Do not change anything here!
  //   You may only change the values of the inputs for testing using the hand tool.
  //   Do not introduce any other input or output pins.
  //   To your logic
  //   OUTPUT SECTION: Do not change anything here!
  //   Do not introduce any other input or output pins.
  //   From your logic
endmodule
