// Logisim project H2.circ as structural Verilog: 2 circuits, main circuit P2
module P2 (
  input  S1,
  input  S0,
  input  In,
  output S1n,
  output S0n,
  output Out
);

  wire and_1_out, and_2_out, and_3_out, and_4_out, and_5_out, and_6_out, and_7_out;

  and and_1 (and_1_out, ~S1, ~S0, ~In);  // AND_Gate
  and and_2 (and_2_out, ~S1, ~S0, In);  // AND_Gate
  and and_3 (and_3_out, ~S1, S0, ~In);  // AND_Gate
  and and_4 (and_4_out, ~S1, S0, In);  // AND_Gate
  and and_5 (and_5_out, S1, ~S0, ~In);  // AND_Gate
  and and_6 (and_6_out, S1, S0, ~In);  // AND_Gate
  and and_7 (and_7_out, S1, S0, In);
  or or_1 (S1n, and_6_out, and_1_out, and_4_out, and_5_out);
  or or_2 (S0n, and_2_out, and_4_out, and_5_out);
  or or_3 (Out, and_2_out, and_3_out, and_5_out, and_6_out, and_7_out);

  // Notes on the sheet:
  //   PROBLEM 2: IMPLEMENTING A STATE TABLE
  //   INPUT SECTION: Do not change anything here!
  //   You may only change the values of the inputs for testing using the hand tool.
  //   Do not introduce any other input or output pins in the circuit.
  //   To your logic
  //   OUTPUT SECTION: Do not change anything here!
  //   Do not introduce any other input or output pins in the circuit.
  //   From your logic
endmodule

module P3 (
  input  In,
  output Out
);

  wire and_1_out, and_2_out, and_3_out, and_4_out, and_5_out, and_6_out, and_7_out, and_8_out, and_9_out,
       and_10_out, and_11_out, clock_1_out, or_1_out, or_2_out, or_3_out, S0_q, S1_q, S2_q;

  and and_1 (and_1_out, ~S2_q, ~S1_q, ~S0_q, ~In);  // AND_Gate
  and and_2 (and_2_out, ~S2_q, ~S1_q, S0_q, ~In);  // AND_Gate
  and and_3 (and_3_out, ~S2_q, ~S1_q, S0_q, In);  // AND_Gate
  and and_4 (and_4_out, ~S2_q, S1_q, ~S0_q, ~In);  // AND_Gate
  and and_5 (and_5_out, ~S2_q, S1_q, S0_q, ~In);  // AND_Gate
  and and_6 (and_6_out, ~S2_q, S1_q, S0_q, In);  // AND_Gate
  and and_7 (and_7_out, S2_q, ~S1_q, ~S0_q, ~In);  // AND_Gate
  and and_8 (and_8_out, S2_q, ~S1_q, S0_q, ~In);  // AND_Gate
  and and_9 (and_9_out, S2_q, ~S1_q, S0_q, In);  // AND_Gate
  and and_10 (and_10_out, S2_q, S1_q, ~S0_q, ~In);  // AND_Gate
  and and_11 (and_11_out, S2_q, S1_q, ~S0_q, In);  // AND_Gate
  or or_1 (or_1_out, and_8_out, and_1_out, and_2_out, and_5_out, and_6_out, and_10_out);
  or or_2 (or_2_out, and_6_out, and_7_out, and_9_out);
  or or_3 (or_3_out, and_9_out, and_2_out, and_3_out, and_4_out, and_8_out);
  or u_Out (Out, and_10_out, and_11_out);
  Clock clock_1 (.out(clock_1_out));
  D_Flip_Flop S2 (.clk(clock_1_out), .D(or_1_out), .Q(S2_q));  // open: Qn, preset, en, reset
  D_Flip_Flop S1 (.clk(clock_1_out), .D(or_2_out), .Q(S1_q));  // open: Qn, preset, en, reset
  D_Flip_Flop S0 (.clk(clock_1_out), .D(or_3_out), .Q(S0_q));  // open: Qn, preset, en, reset

  // Notes on the sheet:
  //   PROBLEM 3: IMPLEMENTING A STATE MACHINE
  //   INPUT SECTION: Do not change anything here!
  //   You may only change the values of the inputs for testing using the hand tool.
  //   Do not introduce any other input or output pins in the circuit.
  //   To your logic
  //   OUTPUT SECTION: Do not change anything here!
  //   Do not introduce any other input or output pins in the circuit.
  //   From your logic
endmodule
